// Logisim project regfile.circ as structural Verilog: 1 circuit, main circuit regfile
module regfile (
  input  [4:0] ReadIndex1,
  input  [4:0] ReadIndex2,
  input  [4:0] WriteIndex,
  input  [31:0] WriteData,
  input  RegWEn,
  input  clk,
  output [31:0] ra,
  output [31:0] sp,
  output [31:0] t0,
  output [31:0] t1,
  output [31:0] t2,
  output [31:0] s0,
  output [31:0] s1,
  output [31:0] a0,
  output [31:0] ReadData1,
  output [31:0] ReadData2
);

  wire [31:0] demultiplexer_1_out1, demultiplexer_1_out2, demultiplexer_1_out3, demultiplexer_1_out4,
       demultiplexer_1_out5, demultiplexer_1_out6, demultiplexer_1_out7, demultiplexer_1_out8,
       demultiplexer_1_out9, demultiplexer_1_out10, demultiplexer_1_out11, demultiplexer_1_out12,
       demultiplexer_1_out13, demultiplexer_1_out14, demultiplexer_1_out15, demultiplexer_1_out16,
       demultiplexer_1_out17, demultiplexer_1_out18, demultiplexer_1_out19, demultiplexer_1_out20,
       demultiplexer_1_out21, demultiplexer_1_out22, demultiplexer_1_out23, demultiplexer_1_out24,
       demultiplexer_1_out25, demultiplexer_1_out26, demultiplexer_1_out27, demultiplexer_1_out28,
       demultiplexer_1_out29, demultiplexer_1_out30, demultiplexer_1_out31, x0_q, x3_q, x4_q, x11_q, x12_q,
       x13_q, x14_q, x15_q, x16_q, x17_q, x18_q, x19_q, x20_q, x21_q, x22_q, x23_q, x24_q, x25_q, x26_q,
       x27_q, x28_q, x29_q, x30_q, x31_q;

  Demultiplexer #(.select(5), .width(32)) demultiplexer_1 (
    .out1(demultiplexer_1_out1), .out2(demultiplexer_1_out2), .out3(demultiplexer_1_out3),
    .out4(demultiplexer_1_out4), .out5(demultiplexer_1_out5), .out6(demultiplexer_1_out6),
    .out7(demultiplexer_1_out7), .out8(demultiplexer_1_out8), .out9(demultiplexer_1_out9),
    .out10(demultiplexer_1_out10), .out11(demultiplexer_1_out11), .out12(demultiplexer_1_out12),
    .out13(demultiplexer_1_out13), .out14(demultiplexer_1_out14), .out15(demultiplexer_1_out15),
    .out16(demultiplexer_1_out16), .out17(demultiplexer_1_out17), .out18(demultiplexer_1_out18),
    .out19(demultiplexer_1_out19), .out20(demultiplexer_1_out20), .out21(demultiplexer_1_out21),
    .out22(demultiplexer_1_out22), .out23(demultiplexer_1_out23), .out24(demultiplexer_1_out24),
    .out25(demultiplexer_1_out25), .out26(demultiplexer_1_out26), .out27(demultiplexer_1_out27),
    .out28(demultiplexer_1_out28), .out29(demultiplexer_1_out29), .out30(demultiplexer_1_out30),
    .out31(demultiplexer_1_out31), .in(WriteData), .sel(WriteIndex));  // open: out0
  Register #(.width(32)) x0 (.D({32{1'b0}}), .en(RegWEn), .clk(clk), .Q(x0_q));  // open: clr
  Register #(.width(32)) x1 (.D(demultiplexer_1_out1), .en(RegWEn), .clk(clk), .Q(ra));  // open: clr
  Register #(.width(32)) x2 (.D(demultiplexer_1_out2), .en(RegWEn), .clk(clk), .Q(sp));  // open: clr
  Register #(.width(32)) x3 (.D(demultiplexer_1_out3), .en(RegWEn), .clk(clk), .Q(x3_q));  // open: clr
  Register #(.width(32)) x4 (.D(demultiplexer_1_out4), .en(RegWEn), .clk(clk), .Q(x4_q));  // open: clr
  Register #(.width(32)) x5 (.D(demultiplexer_1_out5), .en(RegWEn), .clk(clk), .Q(t0));  // open: clr
  Register #(.width(32)) x6 (.D(demultiplexer_1_out6), .en(RegWEn), .clk(clk), .Q(t1));  // open: clr
  Register #(.width(32)) x7 (.D(demultiplexer_1_out7), .en(RegWEn), .clk(clk), .Q(t2));  // open: clr
  Register #(.width(32)) x8 (.D(demultiplexer_1_out8), .en(RegWEn), .clk(clk), .Q(s0));  // open: clr
  Register #(.width(32)) x9 (.D(demultiplexer_1_out9), .en(RegWEn), .clk(clk), .Q(s1));  // open: clr
  Register #(.width(32)) x10 (.D(demultiplexer_1_out10), .en(RegWEn), .clk(clk), .Q(a0));  // open: clr
  Register #(.width(32)) x11 (.D(demultiplexer_1_out11), .en(RegWEn), .clk(clk), .Q(x11_q));  // open: clr
  Register #(.width(32)) x12 (.D(demultiplexer_1_out12), .en(RegWEn), .clk(clk), .Q(x12_q));  // open: clr
  Register #(.width(32)) x13 (.D(demultiplexer_1_out13), .en(RegWEn), .clk(clk), .Q(x13_q));  // open: clr
  Register #(.width(32)) x14 (.D(demultiplexer_1_out14), .en(RegWEn), .clk(clk), .Q(x14_q));  // open: clr
  Register #(.width(32)) x15 (.D(demultiplexer_1_out15), .en(RegWEn), .clk(clk), .Q(x15_q));  // open: clr
  Register #(.width(32)) x16 (.D(demultiplexer_1_out16), .en(RegWEn), .clk(clk), .Q(x16_q));  // open: clr
  Register #(.width(32)) x17 (.D(demultiplexer_1_out17), .en(RegWEn), .clk(clk), .Q(x17_q));  // open: clr
  Register #(.width(32)) x18 (.D(demultiplexer_1_out18), .en(RegWEn), .clk(clk), .Q(x18_q));  // open: clr
  Register #(.width(32)) x19 (.D(demultiplexer_1_out19), .en(RegWEn), .clk(clk), .Q(x19_q));  // open: clr
  Register #(.width(32)) x20 (.D(demultiplexer_1_out20), .en(RegWEn), .clk(clk), .Q(x20_q));  // open: clr
  Register #(.width(32)) x21 (.D(demultiplexer_1_out21), .en(RegWEn), .clk(clk), .Q(x21_q));  // open: clr
  Register #(.width(32)) x22 (.D(demultiplexer_1_out22), .en(RegWEn), .clk(clk), .Q(x22_q));  // open: clr
  Register #(.width(32)) x23 (.D(demultiplexer_1_out23), .en(RegWEn), .clk(clk), .Q(x23_q));  // open: clr
  Register #(.width(32)) x24 (.D(demultiplexer_1_out24), .en(RegWEn), .clk(clk), .Q(x24_q));  // open: clr
  Register #(.width(32)) x25 (.D(demultiplexer_1_out25), .en(RegWEn), .clk(clk), .Q(x25_q));  // open: clr
  Register #(.width(32)) x26 (.D(demultiplexer_1_out26), .en(RegWEn), .clk(clk), .Q(x26_q));  // open: clr
  Register #(.width(32)) x27 (.D(demultiplexer_1_out27), .en(RegWEn), .clk(clk), .Q(x27_q));  // open: clr
  Register #(.width(32)) x28 (.D(demultiplexer_1_out28), .en(RegWEn), .clk(clk), .Q(x28_q));  // open: clr
  Register #(.width(32)) x29 (.D(demultiplexer_1_out29), .en(RegWEn), .clk(clk), .Q(x29_q));  // open: clr
  Register #(.width(32)) x30 (.D(demultiplexer_1_out30), .en(RegWEn), .clk(clk), .Q(x30_q));  // open: clr
  Register #(.width(32)) x31 (.D(demultiplexer_1_out31), .en(RegWEn), .clk(clk), .Q(x31_q));  // open: clr
  Multiplexer #(.select(5), .width(32)) multiplexer_1 (
    .in0(x0_q), .in1(ra), .in2(sp), .in3(x3_q), .in4(x4_q), .in5(t0), .in6(t1), .in7(t2), .in8(s0), .in9(s1),
    .in10(a0), .in11(x11_q), .in12(x12_q), .in13(x13_q), .in14(x14_q), .in15(x15_q), .in16(x16_q),
    .in17(x17_q), .in18(x18_q), .in19(x19_q), .in20(x20_q), .in21(x21_q), .in22(x22_q), .in23(x23_q),
    .in24(x24_q), .in25(x25_q), .in26(x26_q), .in27(x27_q), .in28(x28_q), .in29(x29_q), .in30(x30_q),
    .in31(x31_q), .out(ReadData1), .sel(ReadIndex1));
  Multiplexer #(.select(5), .width(32)) multiplexer_2 (
    .in0(x0_q), .in1(ra), .in2(sp), .in3(x3_q), .in4(x4_q), .in5(t0), .in6(t1), .in7(t2), .in8(s0), .in9(s1),
    .in10(a0), .in11(x11_q), .in12(x12_q), .in13(x13_q), .in14(x14_q), .in15(x15_q), .in16(x16_q),
    .in17(x17_q), .in18(x18_q), .in19(x19_q), .in20(x20_q), .in21(x21_q), .in22(x22_q), .in23(x23_q),
    .in24(x24_q), .in25(x25_q), .in26(x26_q), .in27(x27_q), .in28(x28_q), .in29(x29_q), .in30(x30_q),
    .in31(x31_q), .out(ReadData2), .sel(ReadIndex2));

  // Notes on the sheet:
  //   INPUTS to your circuit
  //   DON'T CHANGE THE LOCATIONS OF THE INPUTS AND OUTPUTS!
  //   These are DEBUG/TEST outputs from your circuit.
  //   OUTPUTS from your circuit
endmodule
